// Logisim project control_logic.circ as structural Verilog: 1 circuit, main circuit control_logic
module control_logic (
  input  [31:0] inst,
  input  BrEq,
  input  BrLt,
  output PCSel,
  output RegWEn,
  output [2:0] ImmSel,
  output BrUn,
  output ASel,
  output BSel,
  output [3:0] ALUSel,
  output MemRW,
  output [1:0] WBSel,
  output CSRSel,
  output CSRWen,
  output [1:0] loadSel
);

  wire b, comparator_4_eq, comparator_5_eq, comparator_8_eq, comparator_9_eq, comparator_14_eq,
       comparator_15_eq, h, load, typeB, typeI, typeJ, typeR, typeU, useALU, w;
  wire [1:0] multiplexer_12_out;
  wire [2:0] ALUSel0, multiplexer_1_out, multiplexer_2_out, multiplexer_6_out, multiplexer_8_out;
  wire [3:0] multiplexer_3_out, multiplexer_4_out, multiplexer_5_out, multiplexer_7_out;

  Comparator #(.width(7)) comparator_1 (.a(inst[6:0]), .b(7'b1100011), .eq(typeB));  // open: gt, lt
  Comparator #(.width(7)) comparator_2 (.a(inst[6:0]), .b(7'b0110011), .eq(typeR));  // open: gt, lt
  Comparator #(.width(7)) comparator_3 (.a(inst[6:0]), .b(7'b0000011), .eq(load));  // open: gt, lt
  Comparator #(.width(7)) comparator_4 (.a(inst[6:0]), .b(7'b1100111), .eq(comparator_4_eq));  // open: gt, lt
  Comparator #(.width(7)) comparator_5 (.a(inst[6:0]), .b(7'b0010011), .eq(comparator_5_eq));  // open: gt, lt
  Comparator #(.width(7)) comparator_6 (.a(inst[6:0]), .b(7'b0100011), .eq(MemRW));  // open: gt, lt
  Comparator #(.width(7)) comparator_7 (.a(inst[6:0]), .b(7'b1100011), .eq(typeB));  // open: gt, lt
  Comparator #(.width(7)) comparator_8 (.a(inst[6:0]), .b(7'b0110111), .eq(comparator_8_eq));  // open: gt, lt
  Comparator #(.width(7)) comparator_9 (.a(inst[6:0]), .b(7'b0010111), .eq(comparator_9_eq));  // open: gt, lt
  Comparator #(.width(7)) comparator_10 (.a(inst[6:0]), .b(7'b1101111), .eq(typeJ));  // open: gt, lt
  or or_1 (typeI, load, comparator_4_eq, comparator_5_eq);
  or or_2 (typeU, comparator_8_eq, comparator_9_eq);
  Multiplexer #(.enable("false"), .width(3)) multiplexer_1 (
    .in0(3'b000), .in1(3'b001), .out(multiplexer_1_out), .sel(typeI));
  Multiplexer #(.enable("false"), .width(3)) multiplexer_2 (
    .in0(multiplexer_1_out), .in1(3'b010), .out(multiplexer_2_out), .sel(MemRW));
  Multiplexer #(.enable("false"), .select(3), .width(4)) multiplexer_3 (
    .in0(4'b0000), .in1(4'b0110), .in2(4'b0111), .in4(4'b0011), .in5(4'b0100), .in6(4'b0010), .in7(4'b0001),
    .out(multiplexer_3_out), .sel(inst[14:12]));  // open: in3
  Multiplexer #(.enable("false"), .select(3), .width(4)) multiplexer_4 (
    .in0(4'b1100), .in5(4'b0101), .out(multiplexer_4_out), .sel(inst[14:12]));  // open: in1, in2, in3, in4, in6, in7
  Multiplexer #(.enable("false"), .select(3), .width(4)) multiplexer_5 (
    .in0(4'b1010), .in1(4'b1110), .in3(4'b1011), .out(multiplexer_5_out), .sel(inst[14:12]));  // open: in2, in4, in5, in6, in7
  Multiplexer #(.enable("false"), .width(3)) multiplexer_6 (
    .in0(multiplexer_2_out), .in1(3'b011), .out(multiplexer_6_out), .sel(typeB));
  Multiplexer #(.enable("false"), .select(3), .width(4)) multiplexer_7 (
    .in1(multiplexer_3_out), .in2(multiplexer_4_out), .in4(multiplexer_5_out), .out(multiplexer_7_out),
    .sel(ALUSel0));  // open: in0, in3, in5, in6, in7
  Multiplexer #(.enable("false"), .width(3)) multiplexer_8 (
    .in0(multiplexer_6_out), .in1(3'b100), .out(multiplexer_8_out), .sel(typeU));
  Comparator #(.width(7)) comparator_11 (.a(inst[31:25]), .b({7{1'b0}}), .eq(ALUSel0[0]));  // open: gt, lt
  Comparator #(.width(7)) comparator_12 (.a(inst[31:25]), .b(7'b0100000), .eq(ALUSel0[1]));  // open: gt, lt
  Comparator #(.width(7)) comparator_13 (.a(inst[31:25]), .b(7'b0000001), .eq(ALUSel0[2]));  // open: gt, lt
  Multiplexer #(.enable("false"), .width(4)) multiplexer_9 (
    .in0(4'b0000), .in1(multiplexer_7_out), .out(ALUSel), .sel(useALU));
  Comparator #(.width(7)) comparator_14 (.a(inst[6:0]), .b(7'b0110011), .eq(comparator_14_eq));  // open: gt, lt
  Comparator #(.width(7)) comparator_15 (.a(inst[6:0]), .b(7'b0010011), .eq(comparator_15_eq));  // open: gt, lt
  Multiplexer #(.enable("false"), .width(3)) multiplexer_10 (
    .in0(multiplexer_8_out), .in1(3'b101), .out(ImmSel), .sel(typeJ));
  or or_3 (useALU, comparator_14_eq, comparator_15_eq);
  Multiplexer #(.enable("false"), .width(2)) multiplexer_11 (.in0(2'b00), .in1(2'b01), .out(WBSel), .sel(load));
  or or_4 (BSel, MemRW, typeI);
  Comparator #(.width(3)) comparator_16 (.a(inst[14:12]), .b(3'b000), .eq(b));  // open: gt, lt
  Comparator #(.width(3)) comparator_17 (.a(inst[14:12]), .b(3'b001), .eq(h));  // open: gt, lt
  Comparator #(.width(3)) comparator_18 (.a(inst[14:12]), .b(3'b010), .eq(w));  // open: gt, lt
  Multiplexer #(.enable("false"), .width(2)) multiplexer_12 (
    .in0(2'b10), .in1(2'b00), .out(multiplexer_12_out), .sel(b));
  or or_5 (RegWEn, typeI, typeR, typeU, typeJ);
  Multiplexer #(.enable("false"), .width(2)) multiplexer_13 (
    .in0(multiplexer_12_out), .in1(2'b01), .out(loadSel), .sel(h));

  // Other names for the same wires on the sheet: opcode[6:0] = inst[6:0]; rd[4:0] = inst[11:7];
  //   funct3[2:0] = inst[14:12]; rs1[4:0] = inst[19:15]; rs2[4:0] = inst[24:20]; funct7[6:0] = inst[31:25];
  //   typeS = MemRW

  // Notes on the sheet:
  //   INPUTS to your circuit
  //   DON'T CHANGE THE LOCATIONS OF THE INPUTS AND OUTPUTS!
  //   OUTPUT from your circuit
endmodule
