// Logisim project cpu.circ as structural Verilog: 1 circuit, main circuit cpu
module cpu (
  input  clk,
  input  [31:0] INSTRUCTION,
  input  [31:0] READ_DATA,
  output [31:0] WRITE_ADDRESS,
  output [31:0] PROGRAM_COUNTER,
  output [31:0] ra,
  output [31:0] sp,
  output [31:0] t0,
  output [31:0] t1,
  output [31:0] t2,
  output [31:0] s0,
  output [31:0] s1,
  output [31:0] a0,
  output [31:0] tohost,
  output [3:0] WRITE_ENABLE,
  output [31:0] WRITE_DATA
);

  wire BSel, MenRW, RegWEn;
  wire [1:0] loadSel, WBSel;
  wire [2:0] funct3, ImmSel;
  wire [3:0] ALUSel, multiplexer_2_out;
  wire [6:0] funct7;
  wire [7:0] bit_extender_1_out;
  wire [15:0] bit_extender_3_out;
  wire [24:0] INSTRUCTION_ID;
  wire [31:0] adder_1_out, bit_extender_2_out, bit_extender_4_out, Imm, multiplexer_1_out,
       PROGRAM_COUNTER_ID, Read_Data_1, SAVE_DATA, WriteData;

  Adder #(.width(32)) adder_1 (.a(PROGRAM_COUNTER), .b(32'h4), .out(adder_1_out));  // open: cin, cout
  Register #(.width(32)) PC (.D(adder_1_out), .clk(clk), .Q(PROGRAM_COUNTER));  // open: en, clr
  Register #(.width(32)) register_1 (.D(PROGRAM_COUNTER), .clk(clk), .Q(PROGRAM_COUNTER_ID));  // open: en, clr
  Register #(.width(32)) register_2 (
    .D(INSTRUCTION), .clk(clk), .Q({funct7, INSTRUCTION_ID[24:15], funct3, INSTRUCTION_ID[11:0]}));  // open: en, clr
  imm_gen imm_gen_1 (.inst({funct7, INSTRUCTION_ID[24:15], funct3, INSTRUCTION_ID[11:0]}), .ImmSel(ImmSel), .imm(Imm));
  control_logic control_logic_1 (
    .loadSel(loadSel), .RegWEn(RegWEn), .ImmSel(ImmSel), .BSel(BSel), .ALUSel(ALUSel), .MemRW(MenRW),
    .WBSel(WBSel), .inst({funct7, INSTRUCTION_ID[24:15], funct3, INSTRUCTION_ID[11:0]}));  // open: CSRWen, PCSel, BrUn, ASel, CSRSel, BrEq, BrLt
  regfile regfile_1 (
    .rs1(INSTRUCTION_ID[19:15]), .rs2(INSTRUCTION_ID[24:20]), .rd(INSTRUCTION_ID[11:7]),
    .Write_Data(WriteData), .RegWEn(RegWEn), .clk(clk), .ra(ra), .sp(sp), .t0(t0), .t1(t1), .t2(t2), .s0(s0),
    .s1(s1), .a0(a0), .Read_Data_1(Read_Data_1), .Read_Data_2(WRITE_DATA));
  // branch_comp branch_comp_1: pin names not known
  Multiplexer #(.enable("false"), .width(32)) multiplexer_1 (
    .in0(WRITE_DATA), .in1(Imm), .out(multiplexer_1_out), .sel(BSel));
  csr csr_1 (.tohost(tohost));  // open: CSR_address, CSR_din, CSR_WE, clk
  alu alu_1 (.Result(WRITE_ADDRESS), .A(Read_Data_1), .B(multiplexer_1_out), .ALUSel(ALUSel));
  Multiplexer #(.enable("false"), .select(2), .width(4)) multiplexer_2 (
    .in0(4'b0001), .in1(4'b0011), .in2(4'b1111), .out(multiplexer_2_out), .sel(loadSel));  // open: in3
  Multiplexer #(.enable("false"), .select(2), .width(32)) multiplexer_3 (
    .in0(WRITE_ADDRESS), .in1(SAVE_DATA), .out(WriteData), .sel(WBSel));  // open: in2, in3
  Bit_Extender #(.in_width(32), .out_width(8), .\type ("zero")) bit_extender_1 (
    .in(READ_DATA), .out(bit_extender_1_out));
  assign bit_extender_2_out = {{24{bit_extender_1_out[7]}}, bit_extender_1_out};  // Bit_Extender bit_extender_2
  Bit_Extender #(.in_width(32), .\type ("zero")) bit_extender_3 (.in(READ_DATA), .out(bit_extender_3_out));
  assign bit_extender_4_out = {{16{bit_extender_3_out[15]}}, bit_extender_3_out};  // Bit_Extender bit_extender_4
  Multiplexer #(.enable("false"), .width(4)) multiplexer_4 (
    .in0(4'b0000), .in1(multiplexer_2_out), .out(WRITE_ENABLE), .sel(MenRW));
  Multiplexer #(.enable("false"), .select(2), .width(32)) multiplexer_5 (
    .in0(bit_extender_2_out), .in1(bit_extender_4_out), .in2(READ_DATA), .out(SAVE_DATA), .sel(loadSel));  // open: in3

  // Other names for the same wires on the sheet: ALU_Res[31:0] = WRITE_ADDRESS; opcode[6:0] = INSTRUCTION_ID[6:0];
  //   rd[4:0] = INSTRUCTION_ID[11:7]; INSTRUCTION_ID (some bits) = {funct7, funct3}; rs1[4:0] = INSTRUCTION_ID[19:15];
  //   rs2[4:0] = INSTRUCTION_ID[24:20]; Read_Data_2[31:0] = WRITE_DATA

  // Notes on the sheet:
  //   Output to IMEM
  //   IMEM (do **NOT** move this)
  //   Inputs from IMEM
  //   It is OK to move the PC, RegFile, ALU, MEM, Branch Comp, Imm Gen, and Control Logic to wherever is most convenient for you when constructing your CPU, and to delete this text
  //   Inputs/Outputs for testing. Do **NOT** move these.
  //   Outputs To DMEM
  //   DMEM (do **NOT** move this)
  //   Inputs From DMEM
endmodule
